# Fritzing sketch Fritzing Sketch Source File (saved by Fritzing 0.9.3b)
breadboards: 1

parts:
  Part2 = IR Receiver Breakout [package=PCB]
  LED1 = LED - 5mm [color="Red (633nm)" package="5 mm [THT]"]
  LED2 = LED - 5mm [color="Red (633nm)" package="5 mm [THT]"]
  R1 = Resistor [tolerance=±5% resistance=220 package="2512 [SMD]"]
  R2 = Resistor [tolerance=±5% resistance=220 package="2010 [SMD]"]
  Part3 = Arduino Uno (Rev3) - ICSP
  J1 = Basic Servo

nets:
  GND: Part2.GND, LED1.cathode, LED2.cathode, Part3.GND, J1.gnd
  VCC: Part2.VCC, Part3.5V, J1.vcc
  N1: Part2.SIGNAL, Part3.D11_PWM/MOSI
  N2: LED1.anode, R1.Pin_0
  N3: LED2.anode, R2.Pin_0
  N4: R1.Pin_1, Part3.D6_PWM
  N5: R2.Pin_1, Part3.D7
  N6: Part3.D10_PWM/SS, J1.pulse

notes:
  GND - Green
  VCC - Orange
  GPIO - Blue
  Developed By Web Dev Fusion
  https://www.webdevfusion.com

custom parts:
  IR Receiver Breakout: Description: This is a very small infrared receiver based on the TSOP85 receiver from Vishay. This receiver has all the filtering and 38kHz demodulation built into the unit. Simply point a IR remote at the receiver, hit a button, and you'll see a stream of 1s and 0s out of the data pin. Documents: Datasheet Schematic Consumer IR Information
